# Fritzing sketch Test_water_sensor (saved by Fritzing 0.9.3b)
breadboards: 1

parts:
  Water_Level_Sensor = Water Level Sensor
  KY-016_3_color_LED_module = KY-016 RGB Full Color LED Module [package="Breakout board"]
  Componente1 = Arduino Nano (Rev3.0)

nets:
  N1: Water_Level_Sensor.SIG, Componente1.A0
  VCC: Water_Level_Sensor.VCC, Componente1.5V
  GND: Water_Level_Sensor.GND, KY-016_3_color_LED_module.-, Componente1.GND
  N2: KY-016_3_color_LED_module.R, Componente1.D2
  N3: KY-016_3_color_LED_module.G, Componente1.D3

notes:
  Test Water sensor
  By www.adrirobot.it

custom parts:
  Water Level Sensor: A water level sensor. This sensor operates at 3V to 5V. The Sig (signal) pin outputs an analogue signal that is in proportion to the amount of water in contact with the sensor.
  KY-016 RGB Full Color LED Module: KY-016 Arduino full color 5mm RGB LED, different colors can be obtained by mixing the three primary colors.
