# Fritzing sketch DiseñoFritzingProyecto (saved by Fritzing 0.9.4)
breadboards: 1

parts:
  Parte2 = Arduino Mega 2560 (Rev3)
  LCD2004-I2C1 = LCD2004-I2C
  R1 = Resistor [tolerance=±5% resistance=220 package=THT]
  R2 = Resistor [tolerance=±5% resistance=220 package=THT]
  J1 = Piezo Speaker
  DHT1 = Humidity and Temperature Sensor DHT11
  LED2 = LEDs [package=led10mm]
  LED1 = LEDs [package=led10mm]
  Sensor_de_Agua = Water Level Sensor
  KY-1 = Keyes Relay [package=THT]
  M1 = DC Motor
  HC-SR04_Sensor_1 = HC-SR04 Ultrasonic Distance Sensor
  X2 = USB Connectors [package=usb-a-s-nosilk]
  X3 = USB Connectors [package=usb-a-pcb]  # not connected

nets:
  N1: Parte2.A2, Sensor_de_Agua.SIG
  N2: Parte2.A3, DHT1.Data-signal
  N3: Parte2.D21/SCL, LCD2004-I2C1.SCL
  5V: Parte2.5V, HC-SR04_Sensor_1.VCC
  GND: Parte2.GND, J1.pin1, LED2.C, LED1.C, HC-SR04_Sensor_1.GND
  N4: Parte2.D2_PWM, R1.Pin_0
  N5: Parte2.D3_PWM, R2.Pin_0
  N6: Parte2.D4_PWM, J1.pin2
  N7: Parte2.D5_PWM, HC-SR04_Sensor_1.ECHO
  N8: Parte2.D7_PWM, KY-1.signal
  N9: R1.Pin_1, LED2.A
  N10: R2.Pin_1, LED1.A
  N11: KY-1.C, X2.D-
  N12: KY-1.NO, M1.pin_1
  N13: M1.pin_2, X2.D+

notes:
  ProyectoSistemaControlTanqueAgua
  Andrés Weitzel
  Lcd con i2c
  Buzzer
  Leds
  DHT11(Modulo/3 in)
  Sección Tanque de Agua
  Sección Sala de Control
  Sensor Ultrasonico
  Sensor de Agua
  Relé(Normal Abierto)
  Bomba de Agua
  Alimentacion(Orientarse al Consumo)
  (Solo  para Bomba)
  Entrada USB Powerbank

custom parts:
  LCD2004-I2C: A standard character display with 4x20 characters. Comes in many colors with LCM2004 IIC attached.
  Humidity and Temperature Sensor DHT11: Digital relative humidity & temperature sensor DHT11
  Water Level Sensor: A water level sensor. This sensor operates at 3V to 5V. The Sig (signal) pin outputs an analogue signal that is in proportion to the amount of water in contact with the sensor.
  Keyes Relay: The Keyes 5V relay module is suitable for SCM development, home appliance control. It uses a 5V~12V TIL control signal which can control DC / AC signal.
